# Fritzing sketch Lab1 part A sketch (saved by Fritzing 0.9.4)
breadboards: 1

parts:
  U1 = 7400 4 x 2 Input NAND Gate [part_number=7400 package="DIP (Dual Inline) [THT]"]

nets:
  N1: U1.B1, U1.Q2, U1.A2
  N2: U1.Q1, U1.B3
  N3: U1.B2, U1.A4
  N4: U1.Q3, U1.Q4

notes:
  Input A
  Input B
  Input C
  Output Z
