# Fritzing sketch Lab1 part B sketch (saved by Fritzing 0.9.4)
breadboards: 1

parts:
  U1 = 7400 4 x 2 Input NAND Gate [part_number=7400 package="DIP (Dual Inline) [THT]"]
  U2 = 7410 3 x 3 Input NAND Gate [part_number=7410 package="DIP (Dual Inline) [THT]"]
  part = 7400 4 x 2 Input NAND Gate [part_number=7400 package="DIP (Dual Inline) [THT]"]  # not connected
  part_2 = 7410 3 x 3 Input NAND Gate [part_number=7410 package="DIP (Dual Inline) [THT]"]  # not connected

nets:
  N1: U1.A1, U1.Q3
  N2: U1.B1, U1.Q2, U1.A2
  N3: U1.Q1, U2.A1
  N4: U1.B2, U1.A4
  GND: U1.GND, U2.GND
  N5: U1.A3, U2.B4
  N6: U1.B3, U1.B4
  N7: U1.Q4, U2.B1
  VDD: U1.VDD, U2.VDD

notes:
  Input A
  Input B
  Input C
  Output Z

custom parts:
  7410 3 x 3 Input NAND Gate: 7410 3 x 2 Input NAND Gate
